# Fritzing sketch LCD-TMP-Counter (saved by Fritzing 0.9.3b)
breadboards: 1

parts:
  LCD1 = LCD screen
  R1 = Rotary Potentiometer (Small) [maximum_resistance=100kΩ package=THT]
  T1 = LM35 Temperature Sensor [package="TO92 [THT]"]
  Bauteil1 = Arduino Uno (Rev3)
  R2 = Resistor [tolerance=±5% resistance=220 package=THT]

nets:
  GND: LCD1.VSS, LCD1.R/W, LCD1.LED-, R1.leg2, T1.GND, Bauteil1.GND
  VDD: LCD1.VDD, R1.leg1, T1.+Vs, Bauteil1.5V, R2.Pin_1
  N1: LCD1.V0, R1.wiper
  N2: LCD1.RS, Bauteil1.D12/MISO
  N3: LCD1.E, Bauteil1.D11_PWM/MOSI
  N4: LCD1.DB4, Bauteil1.D5_PWM
  N5: LCD1.DB5, Bauteil1.D4
  N6: LCD1.DB6, Bauteil1.D3_PWM
  N7: LCD1.DB7, Bauteil1.D2
  N8: LCD1.LED+, R2.Pin_0
  N9: T1.Vout, Bauteil1.A0
