# Fritzing sketch LEDS (saved by Fritzing 0.9.3b)
breadboards: 1

parts:
  Bauteil1 = Arduino Uno (Rev3)
  LED1 = LED - 5mm [color="Red (633nm)" package="5 mm [THT]"]
  R1 = Resistor [tolerance=±5% resistance=220 package=THT]
  LED2 = LED - 5mm [color="Red (633nm)" package="5 mm [THT]"]
  R2 = Resistor [tolerance=±5% resistance=220 package=THT]
  LED3 = LED - 5mm [color="Red (633nm)" package="5 mm [THT]"]
  R3 = Resistor [tolerance=±5% resistance=220 package=THT]
  LED4 = LED - 5mm [color="Red (633nm)" package="5 mm [THT]"]
  R4 = Resistor [tolerance=±5% resistance=220 package=THT]
  S1 = Pushbutton [package="[THT]"]
  R5 = Resistor [tolerance=±5% resistance=10k package=THT]

nets:
  N1: Bauteil1.D2, R5.Pin_1
  N2: Bauteil1.D4, R1.Pin_1
  N3: Bauteil1.D5_PWM, R2.Pin_1
  N4: Bauteil1.D6_PWM, R3.Pin_1
  N5: Bauteil1.D7, R4.Pin_1
  N6: Bauteil1.5V, S1.Pin_1, S1.Pin_2
  N7: Bauteil1.GND, LED1.anode, LED2.anode, LED3.anode
  N8: LED1.cathode, R1.Pin_0
  N9: LED2.cathode, R2.Pin_0
  N10: LED3.cathode, R3.Pin_0
  N11: LED4.cathode, R4.Pin_0
  N12: S1.Pin_3, S1.Pin_4, R5.Pin_0
