# Fritzing sketch digital-tmp-shiftregister (saved by Fritzing 0.9.3b)
circuit board: 8.46667cm x 5.64444cm
breadboards: 1

parts:
  DI1 = 7-Segment LED Display [package=THT]
  DI2 = 7-Segment LED Display [package=THT]
  T1 = LM35 Temperature Sensor [package="TO92 [THT]"]
  U1 = 74HC595 SMD [package="SO16 [SMD]"]
  Bauteil1 = Arduino Uno (Rev3)
  R2 = Resistor [tolerance=±5% resistance=220 package=THT]
  R3 = Resistor [tolerance=±5% resistance=220 package=THT]
  R4 = Resistor [tolerance=±5% resistance=220 package=THT]
  R5 = Resistor [tolerance=±5% resistance=220 package=THT]
  R6 = Resistor [tolerance=±5% resistance=220 package=THT]
  R7 = Resistor [tolerance=±5% resistance=220 package=THT]
  R8 = Resistor [tolerance=±5% resistance=220 package=THT]
  R9 = Resistor [tolerance=±5% resistance=220 package=THT]
  Q1 = NPN-Transistor [package="TO92 [THT]"]
  Q2 = NPN-Transistor [package="TO92 [THT]"]
  R10 = Resistor [tolerance=±5% resistance=10k package=THT]
  R11 = Resistor [tolerance=±5% resistance=10k package=THT]

nets:
  N1: DI1.cathodeE, DI2.cathodeE, U1.Q6, R7.Pin_0, R7.Pin_1
  N2: DI1.cathodeD, DI2.cathodeD, U1.Q7, R8.Pin_0, R8.Pin_1
  N3: DI1.commAnode, Q1.E
  N4: DI1.cathodeC, DI2.cathodeC, U1.Q0, R9.Pin_0, R9.Pin_1
  N5: DI1.cathodeDP, DI2.cathodeDP, U1.Q1, R2.Pin_0, R2.Pin_1
  N6: DI1.cathodeB, DI2.cathodeB, U1.Q5, R6.Pin_0, R6.Pin_1
  N7: DI1.cathodeA, DI2.cathodeA, U1.Q4, R5.Pin_0, R5.Pin_1
  N8: DI1.cathodeF, DI2.cathodeF, U1.Q3, R4.Pin_0, R4.Pin_1
  N9: DI1.cathodeG, DI2.cathodeG, U1.Q2, R3.Pin_0, R3.Pin_1
  N10: DI2.commAnode#7, Q2.E
  VCC: T1.+Vs, U1.VCC, Bauteil1.3V3
  N11: T1.Vout, Bauteil1.A0
  GND: T1.GND, U1.MR, U1.OE, Bauteil1.GND, Q1.C, Q2.C
  N12: U1.SH_CP, Bauteil1.D4
  N13: U1.ST_CP, Bauteil1.D3_PWM
  N14: U1.DS, Bauteil1.D2
  N15: Bauteil1.D5_PWM, Q1.B, R10.Pin_0, R10.Pin_1
  N16: Bauteil1.D6_PWM, Q2.B, R11.Pin_0, R11.Pin_1
