# Fritzing sketch digital-thermometer (saved by Fritzing 0.9.3b)
circuit board: 8.46667cm x 5.64444cm
breadboards: 1

parts:
  DI1 = 7-Segment LED Display [package=THT]
  DI2 = 7-Segment LED Display [package=THT]
  T1 = LM35 Temperature Sensor [package="TO92 [THT]"]
  Bauteil1 = Arduino Uno (Rev3)
  Q1 = NPN-Transistor [package="TO92 [THT]"]
  Q2 = NPN-Transistor [package="TO92 [THT]"]
  R10 = Resistor [tolerance=±5% resistance=10k package=THT]
  R11 = Resistor [tolerance=±5% resistance=10k package=THT]
  R12 = Resistor [tolerance=±5% resistance=220 package=THT]
  R13 = Resistor [tolerance=±5% resistance=220 package=THT]
  R14 = Resistor [tolerance=±5% resistance=220 package=THT]
  R15 = Resistor [tolerance=±5% resistance=220 package=THT]
  R16 = Resistor [tolerance=±5% resistance=220 package=THT]
  R17 = Resistor [tolerance=±5% resistance=220 package=THT]
  R18 = Resistor [tolerance=±5% resistance=220 package=THT]
  R19 = Resistor [tolerance=±5% resistance=220 package=THT]

nets:
  N1: DI1.cathodeE, DI2.cathodeE, R16.Pin_0
  N2: DI1.cathodeD, DI2.cathodeD, R17.Pin_0
  N3: DI1.cathodeC, DI2.cathodeC, R18.Pin_0
  N4: DI1.cathodeDP, DI2.cathodeDP, R19.Pin_0
  N5: DI1.cathodeB, DI2.cathodeB, R15.Pin_0
  N6: DI1.cathodeA, DI2.cathodeA, R14.Pin_0
  N7: DI1.commAnode#7, Q1.E
  N8: DI1.cathodeF, DI2.cathodeF, R13.Pin_0
  N9: DI1.cathodeG, DI2.cathodeG, R12.Pin_0
  N10: DI2.commAnode#7, Q2.E
  N11: T1.+Vs, Bauteil1.3V3
  N12: T1.Vout, Bauteil1.A0
  GND: T1.GND, Bauteil1.GND, Q1.C, Q2.C
  N13: Bauteil1.D8, R18.Pin_1
  N14: Bauteil1.D9_PWM, R19.Pin_1
  N15: Bauteil1.D10_PWM/SS, Q1.B, R10.Pin_0, R10.Pin_1
  N16: Bauteil1.D11_PWM/MOSI, Q2.B, R11.Pin_0, R11.Pin_1
  N17: Bauteil1.D2, R12.Pin_1
  N18: Bauteil1.D3_PWM, R13.Pin_1
  N19: Bauteil1.D4, R14.Pin_1
  N20: Bauteil1.D5_PWM, R15.Pin_1
  N21: Bauteil1.D6_PWM, R16.Pin_1
  N22: Bauteil1.D7, R17.Pin_1
